# Fritzing sketch connection-diagram (saved by Fritzing 0.9.0b)
circuit board: 3.85576cm x 6.90464cm
breadboards: 1

parts:
  R5 = Resistor [tolerance=±5% resistance=100 package=THT]
  R7 = Resistor [tolerance=±5% resistance=1k package=THT]
  R8 = Resistor [tolerance=±5% resistance=1k package=THT]
  R9 = Resistor [tolerance=±5% resistance=1k package=THT]
  JP2 = Header 3 [package=molex-1x3_lock]
  JP3 = Header 2 [package=molex-1x2_lock]
  JP4 = Header 2 [package=molex-1x2_lock]
  JP5 = Header 2 [package=molex-1x2_lock]
  R10 = Resistor [tolerance=±5% resistance=1k package=THT]
  J2 = male pin header, 2 pins [form="♂ (male)"]
  Bauteil1 = Arduino Nano (Rev3.0)
  C3 = Capacitor Polarized [package=panasonic_g]
  MD09B2 = A4988 Stepper Motor Driver Carrier
  M1 = Stepper Motor - Bipolar
  V1 = DC Power [voltage=12V]  # not connected
  R6 = Resistor [tolerance=±5% resistance=1k package=THT]

nets (from the breadboard view):
  N1: R5.Pin_0, J2.pin2
  N2: R5.Pin_1, JP2.1, Bauteil1.5V
  N3: R7.Pin_0, JP3.2, Bauteil1.D9
  N4: R7.Pin_1, R8.Pin_1, R9.Pin_1, C3.-, MD09B2.GROUND#141, R6.Pin_1
  N5: R8.Pin_0, JP2.2, Bauteil1.D12/MISO
  N6: R9.Pin_0, JP2.3, Bauteil1.D11/MOSI
  N7: JP3.1, Bauteil1.D10, R6.Pin_0
  N8: JP4.1, R10.Pin_1, Bauteil1.D8
  N9: JP5.2, R10.Pin_0, Bauteil1.GND, MD09B2.GROUND#147
  N10: J2.pin1, Bauteil1.RESET
  N11: Bauteil1.D2, MD09B2.RESET
  N12: Bauteil1.D3, MD09B2.MS3
  N13: Bauteil1.D4, MD09B2.MS2
  N14: Bauteil1.D5, MD09B2.MS1
  N15: Bauteil1.D6, MD09B2.Enable
  N16: Bauteil1.A2, MD09B2.SLEEP
  N17: Bauteil1.A1, MD09B2.STEP
  N18: Bauteil1.A0, MD09B2.DIR
  N19: C3.+, MD09B2.VMOT
  N20: MD09B2.OUT_2B, M1.A
  N21: MD09B2.OUT_2A, M1.C
  N22: MD09B2.OUT_1A, M1.B
  N23: MD09B2.OUT_1B, M1.D

custom parts:
  A4988 Stepper Motor Driver Carrier: The Pololu stepper motor driver carrier for the A4988 motor driver integrated circuits. http://www.pololu.com/catalog/product/1182
